// Logisim project cpu.circ as structural Verilog: 6 circuits, main circuit main
module main (
  input  [3:0] OperandA,
  input  [3:0] OperandB,
  input  [3:0] StoreOp,
  input  in_4,
  input  InstrFetchRst
);

  wire and_1_out, and_2_out, and_3_out, and_4_out, and_5_out, and_6_out, and_7_out, clock_1_out,
       instrlendec_1_byte1, instrlendec_1_byte2, instrlendec_1_byte3, not_1_out, or_1_out, or_2_out,
       or_3_out, or_4_out, toverwrite_1_q, toverwrite_2_q, toverwrite_3_q, toverwrite_4_q, undriven,
       undriven_2, undriven_3, undriven_4, undriven_5, undriven_6, undriven_7, undriven_8;
  wire [3:0] alu_1_zero;
  wire [7:0] ADDR_q, alu_1_result, BANK_q, BP_q, controlled_buffer_1_out, controlled_buffer_2_out, IR0_q,
       RegA_q, RegB_q, RegC_q, rom_1_data, SP_q;
  wire [15:0] pc_1_q;

  Clock clock_1 (.out(clock_1_out));
  PC pc_1 (.Overwrite(in_4), .CLK(or_1_out), .Q(pc_1_q));  // open: Addr
  not not_1 (not_1_out, or_4_out);
  and and_1 (and_1_out, not_1_out, clock_1_out);
  or or_1 (or_1_out, and_2_out, and_4_out, and_6_out);
  ROM #(.addrWidth(16)) rom_1 (.addr(pc_1_q), .data(rom_1_data));
  InstrLenDec instrlendec_1 (
    .Instr(IR0_q[7:4]), .Byte3(instrlendec_1_byte3), .Byte2(instrlendec_1_byte2), .Byte1(instrlendec_1_byte1));
  TOverwrite toverwrite_1 (
    .D(1'b1), .Overwrite(InstrFetchRst), .TEnable(toverwrite_1_q), .CLK(and_1_out), .Q(toverwrite_1_q));
  and and_2 (and_2_out, and_1_out, toverwrite_1_q);
  and and_3 (and_3_out, instrlendec_1_byte1, toverwrite_2_q);
  or or_2 (or_2_out, toverwrite_2_q, toverwrite_1_q);
  TOverwrite toverwrite_2 (
    .Overwrite(InstrFetchRst), .TEnable(or_2_out), .CLK(and_1_out), .Q(toverwrite_2_q));  // open: D
  and and_4 (and_4_out, and_1_out, toverwrite_2_q);
  and and_5 (and_5_out, instrlendec_1_byte2, toverwrite_3_q);
  or or_3 (or_3_out, toverwrite_3_q, toverwrite_2_q);
  TOverwrite toverwrite_3 (
    .Overwrite(InstrFetchRst), .TEnable(or_3_out), .CLK(and_1_out), .Q(toverwrite_3_q));  // open: D
  and and_6 (and_6_out, and_1_out, toverwrite_3_q);
  and and_7 (and_7_out, instrlendec_1_byte3, toverwrite_4_q);
  or or_4 (or_4_out, and_3_out, and_5_out, and_7_out);
  TOverwrite toverwrite_4 (
    .Overwrite(InstrFetchRst), .TEnable(toverwrite_3_q), .CLK(and_1_out), .Q(toverwrite_4_q));  // open: D
  RAM #(.addrWidth(16)) ram_1 ();  // open: addr, we, oe, clk, din, dout
  Register IR0 (.D(rom_1_data), .en(toverwrite_1_q), .clk(or_1_out), .Q(IR0_q));  // open: clr
  Register IR1 (.D(rom_1_data), .en(toverwrite_2_q), .clk(or_1_out));  // open: Q, clr
  Register IR2 (.D(rom_1_data), .en(toverwrite_3_q), .clk(or_1_out));  // open: Q, clr
  InstrDecoder instrdecoder_1 (.Instr(IR0_q));  // open: Stop, Add, Sub, CarryEn, BitNAND, Cmp, ImmSmall, Imm, Jmp, JmpZero, JmpNeg, JmpCarry, JmpOver, Push, Pop, Ret, Call
  Register RegA (.D(alu_1_result), .en(undriven), .clk(undriven_8), .Q(RegA_q));  // open: clr
  Controlled_Buffer #(.width(8)) controlled_buffer_1 (.in(RegA_q), .out(controlled_buffer_1_out));  // open: en
  Controlled_Buffer #(.width(8)) controlled_buffer_2 (.in(RegA_q), .out(controlled_buffer_2_out));  // open: en
  Register RegB (.D(alu_1_result), .en(undriven_2), .clk(undriven_8), .Q(RegB_q));  // open: clr
  Controlled_Buffer #(.width(8)) controlled_buffer_3 (.in(RegB_q), .out(controlled_buffer_1_out));  // open: en
  Controlled_Buffer #(.width(8)) controlled_buffer_4 (.in(RegB_q), .out(controlled_buffer_2_out));  // open: en
  Register RegC (.D(alu_1_result), .en(undriven_3), .clk(undriven_8), .Q(RegC_q));  // open: clr
  Controlled_Buffer #(.width(8)) controlled_buffer_5 (.in(RegC_q), .out(controlled_buffer_1_out));  // open: en
  Controlled_Buffer #(.width(8)) controlled_buffer_6 (.in(RegC_q), .out(controlled_buffer_2_out));  // open: en
  Register SP (.D(alu_1_result), .en(undriven_4), .clk(undriven_8), .Q(SP_q));  // open: clr
  Controlled_Buffer #(.width(8)) controlled_buffer_7 (.in(SP_q), .out(controlled_buffer_1_out));  // open: en
  Controlled_Buffer #(.width(8)) controlled_buffer_8 (.in(SP_q), .out(controlled_buffer_2_out));  // open: en
  Register BP (.D(alu_1_result), .en(undriven_5), .clk(undriven_8), .Q(BP_q));  // open: clr
  Decoder #(.select(2)) decoder_1 ();  // open: out0, out1, out2, out3, sel, en
  Controlled_Buffer #(.width(8)) controlled_buffer_9 (.in(BP_q), .out(controlled_buffer_1_out));  // open: en
  Controlled_Buffer #(.width(8)) controlled_buffer_10 (.in(BP_q), .out(controlled_buffer_2_out));  // open: en
  Register BANK (.D(alu_1_result), .en(undriven_6), .clk(undriven_8), .Q(BANK_q));  // open: clr
  Controlled_Buffer #(.width(8)) controlled_buffer_11 (.in(BANK_q), .out(controlled_buffer_1_out));  // open: en
  Controlled_Buffer #(.width(8)) controlled_buffer_12 (.in(BANK_q), .out(controlled_buffer_2_out));  // open: en
  Register ADDR (.D(alu_1_result), .en(undriven_7), .clk(undriven_8), .Q(ADDR_q));  // open: clr
  Controlled_Buffer #(.width(8)) controlled_buffer_13 (.in(ADDR_q), .out(controlled_buffer_1_out));  // open: en
  Controlled_Buffer #(.width(8)) controlled_buffer_14 (.in(ADDR_q), .out(controlled_buffer_2_out));  // open: en
  Register #(.width(4)) FLAGS (.D(alu_1_zero));  // open: en, clk, Q, clr
  ALU alu_1 (
    .A(controlled_buffer_1_out), .B(controlled_buffer_2_out), .Result(alu_1_result), .Zero(alu_1_zero[0]),
    .CarryOut(alu_1_zero[1]), .Overflow(alu_1_zero[2]), .Negative(alu_1_zero[3]));  // open: Passthrough, CarryFlag, CarryEn, Subtract, BitNAND

  // Notes on the sheet:
  //   contents of rom_1 (hex, n*v repeats v):
  //   a0 19 a1 2 40 1
endmodule

module ALU (
  input  Passthrough,
  input  CarryFlag,
  input  CarryEn,
  input  [7:0] A,
  input  [7:0] B,
  input  Subtract,
  input  BitNAND,
  output [7:0] Result,
  output Zero,
  output CarryOut,
  output Overflow,
  output Negative
);

  wire and_1_out, nor_1_out, nor_6_out, nor_11_out, nor_12_out, nor_13_out, nor_14_out, nor_15_out,
       nor_16_out, nor_17_out, not_1_out, not_2_out, not_3_out, not_4_out, not_5_out, not_6_out, not_7_out,
       not_8_out, not_9_out, not_10_out, xor_1_out, xor_2_out, xor_3_out, xor_4_out, xor_5_out, xor_6_out,
       xor_7_out, xor_8_out;
  wire [6:0] adder_1_out;
  wire [7:0] nand_1_out, nor_2_out;

  not not_1 (not_1_out, BitNAND);
  nor nor_1 (nor_1_out, not_1_out, Passthrough);
  xor xor_1 (xor_1_out, B[0], Subtract);
  xor xor_2 (xor_2_out, B[1], Subtract);
  xor xor_3 (xor_3_out, B[2], Subtract);
  xor xor_4 (xor_4_out, B[3], Subtract);
  not not_2 (not_2_out, xor_1_out);
  not not_3 (not_3_out, xor_2_out);
  not not_4 (not_4_out, xor_3_out);
  not not_5 (not_5_out, xor_4_out);
  nor nor_2 (nor_2_out[0], not_2_out, Passthrough);
  nor nor_3 (nor_2_out[1], not_3_out, Passthrough);
  nor nor_4 (nor_2_out[2], not_4_out, Passthrough);
  nor nor_5 (nor_2_out[3], not_5_out, Passthrough);
  nand nand_1 (nand_1_out[0], A[0], B[0]);
  nand nand_2 (nand_1_out[1], A[1], B[1]);
  nand nand_3 (nand_1_out[2], A[2], B[2]);
  nand nand_4 (nand_1_out[3], A[3], B[3]);
  not not_6 (not_6_out, Subtract);
  xor xor_5 (xor_5_out, B[4], Subtract);
  not not_7 (not_7_out, xor_5_out);
  xor xor_6 (xor_6_out, B[5], Subtract);
  not not_8 (not_8_out, xor_6_out);
  xor xor_7 (xor_7_out, B[6], Subtract);
  not not_9 (not_9_out, xor_7_out);
  xor xor_8 (xor_8_out, B[7], Subtract);
  not not_10 (not_10_out, xor_8_out);
  nand nand_5 (nand_1_out[4], A[4], B[4]);
  nand nand_6 (nand_1_out[5], A[5], B[5]);
  nand nand_7 (nand_1_out[6], A[6], B[6]);
  nand nand_8 (nand_1_out[7], A[7], B[7]);
  and and_1 (and_1_out, CarryFlag, CarryEn);
  nor nor_6 (nor_6_out, CarryEn, not_6_out);
  nor nor_7 (nor_2_out[4], not_7_out, Passthrough);
  nor nor_8 (nor_2_out[5], not_8_out, Passthrough);
  nor nor_9 (nor_2_out[6], not_9_out, Passthrough);
  nor nor_10 (nor_2_out[7], not_10_out, Passthrough);
  nor nor_11 (nor_11_out, and_1_out, nor_6_out);
  nor nor_12 (nor_12_out, nor_11_out, Passthrough);
  Adder adder_1 (.a(A), .b(nor_2_out), .out({Negative, adder_1_out}), .cin(nor_12_out), .cout(CarryOut));
  nor nor_13 (nor_13_out, A[7], B[7]);
  Multiplexer #(.width(8)) multiplexer_1 (
    .in0({Negative, adder_1_out}), .in1(nand_1_out), .out(Result), .sel(nor_1_out));
  nor nor_14 (nor_14_out, Result[0], Result[1]);
  nor nor_15 (nor_15_out, Result[4], Result[5]);
  and and_2 (Overflow, Negative, nor_13_out);
  nor nor_16 (nor_16_out, Result[2], Result[3]);
  nor nor_17 (nor_17_out, Result[6], Result[7]);
  and and_3 (Zero, nor_14_out, nor_15_out, nor_16_out, nor_17_out);
endmodule

module TOverwrite (
  input  D,
  input  Overwrite,
  input  TEnable,
  input  CLK,
  output Q
);

  wire and_1_out, and_2_out, nand_1_out, nand_2_out, nand_3_out, nand_4_out, nand_5_out, nand_6_out,
       nor_1_out, nor_3_out, not_1_out, not_2_out, not_3_out, not_4_out, not_5_out;

  not not_1 (not_1_out, CLK);
  not not_2 (not_2_out, not_1_out);
  not not_3 (not_3_out, not_2_out);
  not not_4 (not_4_out, Overwrite);
  and and_1 (and_1_out, TEnable, nor_1_out);
  nor nor_1 (nor_1_out, CLK, not_3_out);
  and and_2 (and_2_out, and_1_out, not_4_out);
  nand nand_1 (nand_1_out, Q, and_2_out);
  nand nand_2 (nand_2_out, and_2_out, nor_3_out);
  not not_5 (not_5_out, D);
  nand nand_3 (nand_3_out, not_5_out, Overwrite);
  nand nand_4 (nand_4_out, D, Overwrite);
  nand nand_5 (nand_5_out, nand_1_out, nand_3_out);
  nand nand_6 (nand_6_out, nand_4_out, nand_2_out);
  nor nor_2 (Q, nand_5_out, nor_3_out);
  nor nor_3 (nor_3_out, Q, nand_6_out);
endmodule

module PC (
  input  [15:0] Addr,
  input  Overwrite,
  input  CLK,
  output [15:0] Q
);

  TOverwrite toverwrite_1 (.D(Addr[0]), .Overwrite(Overwrite), .TEnable(1'b1), .CLK(CLK), .Q(Q[0]));
  TOverwrite toverwrite_2 (.D(Addr[8]), .Overwrite(Overwrite), .TEnable(1'b1), .CLK(Q[7]), .Q(Q[8]));
  TOverwrite toverwrite_3 (.D(Addr[1]), .Overwrite(Overwrite), .TEnable(1'b1), .CLK(Q[0]), .Q(Q[1]));
  TOverwrite toverwrite_4 (.D(Addr[9]), .Overwrite(Overwrite), .TEnable(1'b1), .CLK(Q[8]), .Q(Q[9]));
  TOverwrite toverwrite_5 (.D(Addr[2]), .Overwrite(Overwrite), .TEnable(1'b1), .CLK(Q[1]), .Q(Q[2]));
  TOverwrite toverwrite_6 (.D(Addr[10]), .Overwrite(Overwrite), .TEnable(1'b1), .CLK(Q[9]), .Q(Q[10]));
  TOverwrite toverwrite_7 (.D(Addr[3]), .Overwrite(Overwrite), .TEnable(1'b1), .CLK(Q[2]), .Q(Q[3]));
  TOverwrite toverwrite_8 (.D(Addr[11]), .Overwrite(Overwrite), .TEnable(1'b1), .CLK(Q[10]), .Q(Q[11]));
  TOverwrite toverwrite_9 (.D(Addr[4]), .Overwrite(Overwrite), .TEnable(1'b1), .CLK(Q[3]), .Q(Q[4]));
  TOverwrite toverwrite_10 (.D(Addr[12]), .Overwrite(Overwrite), .TEnable(1'b1), .CLK(Q[11]), .Q(Q[12]));
  TOverwrite toverwrite_11 (.D(Addr[5]), .Overwrite(Overwrite), .TEnable(1'b1), .CLK(Q[4]), .Q(Q[5]));
  TOverwrite toverwrite_12 (.D(Addr[13]), .Overwrite(Overwrite), .TEnable(1'b1), .CLK(Q[12]), .Q(Q[13]));
  TOverwrite toverwrite_13 (.D(Addr[6]), .Overwrite(Overwrite), .TEnable(1'b1), .CLK(Q[5]), .Q(Q[6]));
  TOverwrite toverwrite_14 (.D(Addr[14]), .Overwrite(Overwrite), .TEnable(1'b1), .CLK(Q[13]), .Q(Q[14]));
  TOverwrite toverwrite_15 (.D(Addr[7]), .Overwrite(Overwrite), .TEnable(1'b1), .CLK(Q[6]), .Q(Q[7]));
  TOverwrite toverwrite_16 (.D(Addr[15]), .Overwrite(Overwrite), .TEnable(1'b1), .CLK(Q[14]), .Q(Q[15]));
endmodule

module InstrLenDec (
  input  [3:0] Instr,
  output Byte3,
  output Byte2,
  output Byte1
);

  nor nor_1 (Byte1, Instr[2], Instr[3]);
  and and_1 (Byte3, Instr[1], Instr[2], Instr[3]);
  nor nor_2 (Byte2, Byte3, Byte1);
endmodule

module InstrDecoder (
  input  [7:0] Instr,
  output Stop,
  output Add,
  output Sub,
  output CarryEn,
  output BitNAND,
  output Cmp,
  output ImmSmall,
  output Imm,
  output Jmp,
  output JmpZero,
  output JmpNeg,
  output JmpCarry,
  output JmpOver,
  output Push,
  output Pop,
  output Ret,
  output Call
);

  wire nor_5_out, nor_6_out, nor_7_out, nor_8_out, nor_9_out, nor_10_out, not_1_out, not_2_out, not_3_out,
       not_4_out;

  not not_1 (not_1_out, Instr[4]);
  not not_2 (not_2_out, Instr[5]);
  not not_3 (not_3_out, Instr[6]);
  not not_4 (not_4_out, Instr[7]);
  nor nor_1 (Stop, Instr[7], Instr[6], Instr[5], Instr[4]);
  nor nor_2 (Push, Instr[7], Instr[6], Instr[5], not_1_out);
  nor nor_3 (Pop, Instr[7], Instr[6], not_2_out, Instr[4]);
  nor nor_4 (Ret, Instr[7], Instr[6], not_2_out, not_1_out);
  and and_1 (JmpZero, Jmp, Instr[0]);
  and and_2 (JmpCarry, Jmp, Instr[2]);
  nor nor_5 (nor_5_out, Instr[7], not_3_out, Instr[5], Instr[4]);
  nor nor_6 (nor_6_out, Instr[7], not_3_out, Instr[5], not_1_out);
  and and_3 (JmpNeg, Jmp, Instr[1]);
  and and_4 (JmpOver, Jmp, Instr[3]);
  nor nor_7 (nor_7_out, Instr[7], not_3_out, not_2_out, not_1_out);
  nor nor_8 (nor_8_out, Instr[7], not_3_out, not_2_out, Instr[4]);
  or or_1 (Add, nor_5_out, nor_6_out, nor_8_out);
  nor nor_9 (nor_9_out, not_4_out, Instr[6], Instr[5], Instr[4]);
  nor nor_10 (nor_10_out, not_4_out, Instr[6], Instr[5], not_1_out);
  nor nor_11 (Imm, not_4_out, Instr[6], not_2_out, Instr[4]);
  or or_2 (ImmSmall, nor_10_out, nor_8_out);
  or or_3 (Sub, nor_7_out, nor_9_out, nor_10_out);
  nor nor_12 (BitNAND, not_4_out, Instr[6], not_2_out, not_1_out);
  or or_4 (CarryEn, nor_6_out, nor_9_out);
  nor nor_13 (Cmp, not_4_out, not_3_out, Instr[5], Instr[4]);
  nor nor_14 (Jmp, not_4_out, not_3_out, not_2_out, Instr[4]);
  nor nor_15 (Call, not_4_out, not_3_out, not_2_out, not_1_out);
endmodule
